// Logisim project proccessor.circ as structural Verilog
module HALF_ADDER (
  input  A,
  input  B,
  output SUM,
  output CARRY
);

  xor xor_1 (SUM, A, B);
  and and_1 (CARRY, A, B);
endmodule

module INC_4BIT (
  input  A,
  input  A_1,
  input  A_2,
  input  A_3,
  input  INC,
  output Y,
  output Y_1,
  output Y_2,
  output Y_3,
  output CARRY
);

  wire half_adder_1_carry, half_adder_2_carry, half_adder_3_carry;

  HALF_ADDER half_adder_1 (.A(INC), .B(A), .SUM(Y), .CARRY(half_adder_1_carry));
  HALF_ADDER half_adder_2 (.A(half_adder_1_carry), .B(A_1), .SUM(Y_1), .CARRY(half_adder_2_carry));
  HALF_ADDER half_adder_3 (.A(half_adder_2_carry), .B(A_2), .SUM(Y_2), .CARRY(half_adder_3_carry));
  HALF_ADDER half_adder_4 (.A(half_adder_3_carry), .B(A_3), .SUM(Y_3), .CARRY(CARRY));
endmodule
